// Logisim project 64x8_memory_autofill_ev.circ as structural Verilog: 1 circuit, main circuit main
module main (
  input  in_1,
  output [7:0] out_2
);

  wire and_1_out, and_2_out, and_3_out, and_4_out, ck, cs0, cs1, cs2, cs3, not_1_out, not_2_out, not_3_out,
       not_4_out, not_5_out;
  wire [1:0] count;
  wire [3:0] addr;
  wire [7:0] controlled_buffer_2_out, multiplexer_1_out, ram_1_data, ram_2_data, ram_3_data, ram_4_data;

  and and_1 (and_1_out, ck, cs0);
  and and_2 (and_2_out, ck, cs1);
  and and_3 (and_3_out, ck, cs2);
  and and_4 (and_4_out, ck, cs3);
  RAM #(.addrWidth(4)) ram_1 (.addr(addr), .we(not_1_out), .oe(in_1), .clk(and_1_out), .data(ram_1_data));
  not not_1 (not_1_out, in_1);
  RAM #(.addrWidth(4)) ram_2 (.addr(addr), .we(not_2_out), .oe(in_1), .clk(and_2_out), .data(ram_2_data));
  not not_2 (not_2_out, in_1);
  RAM #(.addrWidth(4)) ram_3 (.addr(addr), .we(not_3_out), .oe(in_1), .clk(and_3_out), .data(ram_3_data));
  not not_3 (not_3_out, in_1);
  RAM #(.addrWidth(4)) ram_4 (.addr(addr), .we(not_4_out), .oe(in_1), .clk(and_4_out), .data(ram_4_data));
  not not_4 (not_4_out, in_1);
  Multiplexer #(.select(2), .width(8), .enable("false")) multiplexer_1 (
    .in0(ram_1_data), .in1(ram_2_data), .in2(ram_3_data), .in3(ram_4_data), .out(multiplexer_1_out),
    .sel(count));
  Demultiplexer #(.select(2), .width(8), .enable("false")) demultiplexer_1 (
    .out0(ram_1_data), .out1(ram_2_data), .out2(ram_3_data), .out3(ram_4_data), .in(controlled_buffer_2_out),
    .sel(count));
  Clock clock_1 (.out(ck));
  assign out_2 = in_1 ? multiplexer_1_out : 8'bz;  // Controlled_Buffer controlled_buffer_1
  not not_5 (not_5_out, in_1);
  assign controlled_buffer_2_out = not_5_out ? {2'b00, addr, count} : 8'bz;  // Controlled_Buffer controlled_buffer_2
  Decoder #(.select(2)) decoder_1 (.out0(cs0), .out1(cs1), .out2(cs2), .out3(cs3), .sel(count));  // open: en
  Counter #(.width(6), .max('h3f)) counter_1 (.clk(ck), .Q({addr, count}));  // open: clr, load, up, count, D, carry

  // Other names for the same wires on the sheet: sel[1:0] = count; count[5:2] = addr; ld = in_1
endmodule
