// Logisim project 8x3_memory_8x1_ev.circ as structural Verilog: 1 circuit, main circuit main
module main (
  input  [2:0] in_1,
  input  in_2,
  input  [2:0] in_3,
  output [2:0] out_4
);

  wire ck, not_1_out, not_2_out, not_3_out, not_4_out;
  wire [2:0] ram_1_data;

  Button button_1 (.out(ck));
  RAM #(.addrWidth(3), .dataWidth(1)) ram_1 (.addr(in_1), .we(not_1_out), .clk(ck), .data(ram_1_data[0]));  // open: oe
  not not_1 (not_1_out, in_2);
  RAM #(.addrWidth(3), .dataWidth(1)) ram_2 (.addr(in_1), .we(not_2_out), .clk(ck), .data(ram_1_data[1]));  // open: oe
  not not_2 (not_2_out, in_2);
  RAM #(.addrWidth(3), .dataWidth(1)) ram_3 (.addr(in_1), .we(not_3_out), .clk(ck), .data(ram_1_data[2]));  // open: oe
  not not_3 (not_3_out, in_2);
  assign ram_1_data = not_4_out ? in_3 : 3'bz;  // Controlled_Buffer controlled_buffer_1
  assign out_4 = in_2 ? ram_1_data : 3'bz;  // Controlled_Buffer controlled_buffer_2
  not not_4 (not_4_out, in_2);

  // Other names for the same wires on the sheet: ld = in_2
endmodule
