// Logisim project ALUs.circ as structural Verilog: 3 circuits, main circuit ALU1bit
module ALU1bit (
  input  INVA,
  input  A,
  input  ENA,
  input  B,
  input  ENB,
  input  F0,
  input  F1,
  input  Cin,
  output Cout,
  output O
);

  wire adder_1_cout, adder_1_out, and_2_out, and_3_out, and_4_out, and_5_out, and_6_out, and_7_out,
       and_8_out, decoder_1_out0, decoder_1_out1, decoder_1_out2, decoder_1_out3, not_1_out, or_1_out,
       xor_1_out;

  Decoder #(.select(2)) decoder_1 (
    .out0(decoder_1_out0), .out1(decoder_1_out1), .out2(decoder_1_out2), .out3(decoder_1_out3), .sel({F1, F0}));  // open: en
  and and_1 (Cout, decoder_1_out3, adder_1_cout);
  and and_2 (and_2_out, A, ENA);
  xor xor_1 (xor_1_out, INVA, and_2_out);
  Adder #(.width(1)) adder_1 (.a(and_6_out), .b(xor_1_out), .out(adder_1_out), .cin(Cin), .cout(adder_1_cout));
  and and_3 (and_3_out, decoder_1_out3, adder_1_out);
  or or_1 (or_1_out, xor_1_out, and_6_out);
  not not_1 (not_1_out, and_6_out);
  and and_4 (and_4_out, decoder_1_out2, not_1_out);
  and and_5 (and_5_out, decoder_1_out1, or_1_out);
  or or_2 (O, and_3_out, and_4_out, and_5_out, and_8_out);
  and and_6 (and_6_out, B, ENB);
  and and_7 (and_7_out, xor_1_out, and_6_out);
  and and_8 (and_8_out, decoder_1_out0, and_7_out);
endmodule

module ALU8bit (
  input  INVA,
  input  [7:0] A,
  input  ENA,
  input  [7:0] B,
  input  ENB,
  input  F0,
  input  F1,
  input  INC,
  output [7:0] O
);

  wire alu1bit_2_cout, alu1bit_3_cout, alu1bit_4_cout, alu1bit_5_cout, alu1bit_6_cout, alu1bit_7_cout,
       alu1bit_8_cout;

  ALU1bit alu1bit_1 (
    .Cin(alu1bit_2_cout), .F0(F0), .B(B[7]), .A(A[7]), .O(O[7]), .INVA(INVA), .ENA(ENA), .ENB(ENB), .F1(F1));  // open: Cout
  ALU1bit alu1bit_2 (
    .Cin(alu1bit_3_cout), .F0(F0), .B(B[6]), .A(A[6]), .Cout(alu1bit_2_cout), .O(O[6]), .INVA(INVA),
    .ENA(ENA), .ENB(ENB), .F1(F1));
  ALU1bit alu1bit_3 (
    .Cin(alu1bit_4_cout), .F0(F0), .B(B[5]), .A(A[5]), .Cout(alu1bit_3_cout), .O(O[5]), .INVA(INVA),
    .ENA(ENA), .ENB(ENB), .F1(F1));
  ALU1bit alu1bit_4 (
    .Cin(alu1bit_5_cout), .F0(F0), .B(B[4]), .A(A[4]), .Cout(alu1bit_4_cout), .O(O[4]), .INVA(INVA),
    .ENA(ENA), .ENB(ENB), .F1(F1));
  ALU1bit alu1bit_5 (
    .Cin(alu1bit_6_cout), .F0(F0), .B(B[3]), .A(A[3]), .Cout(alu1bit_5_cout), .O(O[3]), .INVA(INVA),
    .ENA(ENA), .ENB(ENB), .F1(F1));
  ALU1bit alu1bit_6 (
    .Cin(alu1bit_7_cout), .F0(F0), .B(B[2]), .A(A[2]), .Cout(alu1bit_6_cout), .O(O[2]), .INVA(INVA),
    .ENA(ENA), .ENB(ENB), .F1(F1));
  ALU1bit alu1bit_7 (
    .Cin(alu1bit_8_cout), .F0(F0), .B(B[1]), .A(A[1]), .Cout(alu1bit_7_cout), .O(O[1]), .INVA(INVA),
    .ENA(ENA), .ENB(ENB), .F1(F1));
  ALU1bit alu1bit_8 (
    .Cin(INC), .F0(F0), .B(B[0]), .A(A[0]), .Cout(alu1bit_8_cout), .O(O[0]), .INVA(INVA), .ENA(ENA),
    .ENB(ENB), .F1(F1));

  // Other names for the same wires on the sheet: EA = ENA; EB = ENB; IV = INVA
endmodule

module ALU32bit (
  input  [31:0] A,
  input  [31:0] B,
  input  [5:0] in_3,
  output N,
  output [31:0] O,
  output Z
);

  wire [31:0] adder_1_out, and_1_out, and_2_out, and_3_out, bit_extender_1_out, bit_extender_2_out,
       bit_extender_3_out, not_1_out, or_1_out, xor_1_out;

  assign bit_extender_1_out = {{31{in_3[1]}}, in_3[1]};  // Bit_Extender bit_extender_1
  assign xor_1_out = bit_extender_1_out ^ and_1_out;  // XOR_Gate xor_1, 32 bits wide
  Adder #(.width(32)) adder_1 (.a(and_3_out), .b(xor_1_out), .out(adder_1_out), .cin(in_3[0]));  // open: cout
  assign and_1_out = A & bit_extender_2_out;  // AND_Gate and_1, 32 bits wide
  assign bit_extender_2_out = {{31{in_3[3]}}, in_3[3]};  // Bit_Extender bit_extender_2
  assign and_2_out = and_3_out & xor_1_out;  // AND_Gate and_2, 32 bits wide
  Multiplexer #(.select(2), .width(32), .enable("false")) multiplexer_1 (
    .in0(and_2_out), .in1(or_1_out), .in2(not_1_out), .in3(adder_1_out), .out(O), .sel({in_3[4], in_3[5]}));
  assign bit_extender_3_out = {{31{in_3[2]}}, in_3[2]};  // Bit_Extender bit_extender_3
  assign and_3_out = B & bit_extender_3_out;  // AND_Gate and_3, 32 bits wide
  assign or_1_out = and_3_out | xor_1_out;  // OR_Gate or_1, 32 bits wide
  assign not_1_out = ~and_3_out;  // NOT_Gate not_1, 32 bits wide
  BitSelector #(.width(32)) bitselector_1 (.in(O), .out(N), .sel({5{1'b1}}));
  Comparator #(.width(32)) comparator_1 (.a(O), .b({32{1'b0}}), .eq(Z));  // open: gt, lt

  // Other names for the same wires on the sheet: F0 = in_3[5]; F1 = in_3[4]; INC = in_3[0]; INVA = in_3[1];
  //   ENB = in_3[2]; ENA = in_3[3]
endmodule
