// Logisim project adder.circ as structural Verilog: 1 circuit, main circuit main
module main (
  input  [7:0] in_1,
  input  [7:0] in_2
);

  wire adder_1_out, adder_2_out;

  Adder #(.width(1)) adder_1 (.a(in_1[0]), .b(in_2[0]), .out(adder_1_out));  // open: cin, cout
  Adder #(.width(1)) adder_2 (.a(in_1[1]), .b(in_2[1]), .out(adder_2_out));  // open: cin, cout
  Adder #(.width(1)) adder_3 (.a(in_1[2]), .b(in_2[2]));  // open: out, cin, cout
  Adder #(.width(1)) adder_4 (.a(in_1[3]), .b(in_2[3]));  // open: out, cin, cout
  Adder #(.width(1)) adder_5 (.a(in_1[4]), .b(in_2[4]));  // open: out, cin, cout
  Adder #(.width(1)) adder_6 (.a(in_1[5]), .b(in_2[5]));  // open: out, cin, cout
  Adder #(.width(1)) adder_7 (.a(in_1[6]), .b(in_2[6]));  // open: out, cin, cout
  Adder #(.width(1)) adder_8 (.a(in_1[7]), .b(in_2[7]));  // open: out, cin, cout
  Multiplexer #(.enable("false")) multiplexer_1 ();  // open: in0, in1, out, sel
endmodule
