// Logisim project complicatedthing.circ as structural Verilog: 2 circuits, main circuit ALU1bit
module ALU1bit (
  input  Cin,
  input  INVA,
  input  A,
  input  ENA,
  input  B,
  input  ENB,
  input  F0,
  input  F1,
  output O,
  output Cout
);

  wire adder_1_cout, adder_1_out, and_1_out, and_2_out, and_3_out, and_4_out, and_5_out, and_6_out,
       and_7_out, decoder_1_out0, decoder_1_out1, decoder_1_out2, decoder_1_out3, not_1_out, or_1_out,
       xor_1_out;

  and and_1 (and_1_out, A, ENA);
  xor xor_1 (xor_1_out, INVA, and_1_out);
  and and_2 (and_2_out, B, ENB);
  and and_3 (and_3_out, xor_1_out, and_2_out);
  or or_1 (or_1_out, xor_1_out, and_2_out);
  not not_1 (not_1_out, and_2_out);
  Decoder #(.select(2)) decoder_1 (
    .out0(decoder_1_out0), .out1(decoder_1_out1), .out2(decoder_1_out2), .out3(decoder_1_out3), .sel({F1, F0}));  // open: en
  Adder #(.width(1)) adder_1 (.a(xor_1_out), .b(and_2_out), .out(adder_1_out), .cin(Cin), .cout(adder_1_cout));
  and and_4 (and_4_out, and_3_out, decoder_1_out0);
  and and_5 (and_5_out, or_1_out, decoder_1_out1);
  and and_6 (and_6_out, not_1_out, decoder_1_out2);
  and and_7 (and_7_out, adder_1_out, decoder_1_out3);
  and and_8 (Cout, adder_1_cout, decoder_1_out3);
  or or_2 (O, and_4_out, and_5_out, and_6_out, and_7_out);
endmodule

module ALU8bit (
  input  [7:0] A,
  input  [7:0] B
);

  ALU1bit alu1bit_1 (.A(A[3]), .B(B[3]));  // open: Cin, INVA, ENA, ENB, F0, F1, O, Cout
  ALU1bit alu1bit_2 (.A(A[7]), .B(B[7]));  // open: Cin, INVA, ENA, ENB, F0, F1, O, Cout
  ALU1bit alu1bit_3 (.A(A[2]), .B(B[2]));  // open: Cin, INVA, ENA, ENB, F0, F1, O, Cout
  ALU1bit alu1bit_4 (.A(A[6]), .B(B[6]));  // open: Cin, INVA, ENA, ENB, F0, F1, O, Cout
  ALU1bit alu1bit_5 (.A(A[1]), .B(B[1]));  // open: Cin, INVA, ENA, ENB, F0, F1, O, Cout
  ALU1bit alu1bit_6 (.A(A[5]), .B(B[5]));  // open: Cin, INVA, ENA, ENB, F0, F1, O, Cout
  ALU1bit alu1bit_7 (.A(A[0]), .B(B[0]));  // open: Cin, INVA, ENA, ENB, F0, F1, O, Cout
  ALU1bit alu1bit_8 (.A(A[4]), .B(B[4]));  // open: Cin, INVA, ENA, ENB, F0, F1, O, Cout
endmodule
