// Logisim project mic1CPUv1.circ as structural Verilog: 1 circuit, main circuit main
module main (
  input  C_MAR,
  input  C_MDR,
  input  MDR_B,
  input  C_PC,
  input  PC_B,
  input  MBR_B,
  input  MBRU_B,
  input  C_SP,
  input  SP_B,
  input  C_LV,
  input  LV_B,
  input  C_CPP,
  input  CPP_B,
  input  C_TOS,
  input  TOS_B,
  input  C_OPC,
  input  OPC_B,
  input  C_H,
  input  F0,
  input  F1,
  input  ENA,
  input  ENB,
  input  INVA,
  input  SRA1,
  input  INC,
  input  SLL8
);

  wire alu32bit_1_n, alu32bit_1_z, GO_out, Reset_out;
  wire [7:0] mic1regblocknomem_1_mbr;
  wire [31:0] alu32bit_1_o, mic1regblocknomem_1_abus, mic1regblocknomem_1_bbus, mic1regblocknomem_1_cpp,
       mic1regblocknomem_1_h, mic1regblocknomem_1_lv, mic1regblocknomem_1_mar, mic1regblocknomem_1_mdr,
       mic1regblocknomem_1_opc, mic1regblocknomem_1_pc, mic1regblocknomem_1_sp, mic1regblocknomem_1_tos,
       shiftunit_1_out;

  // Probe on mic1regblocknomem_1_mar
  // Probe on mic1regblocknomem_1_mdr
  // Probe on mic1regblocknomem_1_pc
  // Probe on mic1regblocknomem_1_mbr
  // Probe on mic1regblocknomem_1_sp
  // Probe on mic1regblocknomem_1_lv
  // Probe on mic1regblocknomem_1_cpp
  // Probe on mic1regblocknomem_1_tos
  // Probe on mic1regblocknomem_1_opc
  // Probe on mic1regblocknomem_1_h
  mic1RegBlockNomem mic1regblocknomem_1 (
    .MDR(mic1regblocknomem_1_mdr), .MAR(mic1regblocknomem_1_mar), .C_H(C_H), .OPC_B(OPC_B), .C_OPC(C_OPC),
    .TOS_B(TOS_B), .C_TOS(C_TOS), .CPP_B(CPP_B), .C_CPP(C_CPP), .LV_B(LV_B), .C_LV(C_LV), .RST(Reset_out),
    .CLK(GO_out), .SP_B(SP_B), .C_SP(C_SP), .CBUS(shiftunit_1_out), .MBRU_B(MBRU_B), .MBR_B(MBR_B),
    .PC_B(PC_B), .C_PC(C_PC), .MDR_B(MDR_B), .C_MDR(C_MDR), .C_MAR(C_MAR), .PC(mic1regblocknomem_1_pc),
    .MBR(mic1regblocknomem_1_mbr), .SP(mic1regblocknomem_1_sp), .BBUS(mic1regblocknomem_1_bbus),
    .LV(mic1regblocknomem_1_lv), .CPP(mic1regblocknomem_1_cpp), .TOS(mic1regblocknomem_1_tos),
    .OPC(mic1regblocknomem_1_opc), .H(mic1regblocknomem_1_h), .ABUS(mic1regblocknomem_1_abus));
  ALU32bit alu32bit_1 (
    .A(mic1regblocknomem_1_abus), .O(alu32bit_1_o), .B(mic1regblocknomem_1_bbus), .N(alu32bit_1_n),
    .Z(alu32bit_1_z), .in_3({F0, F1, ENA, ENB, INVA, INC}));
  shiftUnit shiftunit_1 (.SRA1(SRA1), .SLL8(SLL8), .IN(alu32bit_1_o), .OUT(shiftunit_1_out));
  Button Reset (.out(Reset_out));
  LED N (.in(alu32bit_1_n));
  LED Z (.in(alu32bit_1_z));
  Button GO (.out(GO_out));
endmodule
