// Logisim project mic1CPUv2.circ as structural Verilog: 1 circuit, main circuit main
module main (
  input  [31:0] MDRin,
  input  SLL8,
  input  SRA1,
  input  F0,
  input  F1,
  input  ENA,
  input  ENB,
  input  INVA,
  input  INC,
  input  iH,
  input  iOPC,
  input  iTOS,
  input  iCPP,
  input  iLV,
  input  iSP,
  input  iPC,
  input  iMDR,
  input  iMAR,
  input  Write,
  input  Read,
  input  Fetch,
  input  [3:0] B_Bus,
  input  [7:0] MBRin
);

  wire alu32bit_1_n, alu32bit_1_z, decoder_1_out0, decoder_1_out1, decoder_1_out2, decoder_1_out3,
       decoder_1_out4, decoder_1_out5, decoder_1_out6, decoder_1_out7, decoder_1_out8, GO_out, Reset_out;
  wire [7:0] registerblockmem_1_mbr;
  wire [31:0] alu32bit_1_o, registerblockmem_1_abus, registerblockmem_1_bbus, registerblockmem_1_cpp,
       registerblockmem_1_h, registerblockmem_1_lv, registerblockmem_1_mar, registerblockmem_1_mdr,
       registerblockmem_1_opc, registerblockmem_1_pc, registerblockmem_1_sp, registerblockmem_1_tos,
       shiftunit_1_out;

  // Probe on registerblockmem_1_mbr
  // Probe on registerblockmem_1_h
  registerBlockMem registerblockmem_1 (
    .C_H(iH), .C_TOS(iTOS), .C_LV(iLV), .C_SP(iSP), .PC_B(decoder_1_out1), .C_MAR(iMAR),
    .PC(registerblockmem_1_pc), .C_PC(iPC), .CBUS(shiftunit_1_out), .RST(Reset_out), .CPP_B(decoder_1_out6),
    .OPC_B(decoder_1_out8), .SP(registerblockmem_1_sp), .MAR(registerblockmem_1_mar), .TOS_B(decoder_1_out7),
    .LV_B(decoder_1_out5), .SP_B(decoder_1_out4), .MBR_B(decoder_1_out2), .C_MDR(iMDR),
    .MBR(registerblockmem_1_mbr), .MDR_B(decoder_1_out0), .MBRU_B(decoder_1_out3), .CLK(GO_out),
    .C_CPP(iCPP), .C_OPC(iOPC), .MDR(registerblockmem_1_mdr), .BBUS(registerblockmem_1_bbus),
    .LV(registerblockmem_1_lv), .CPP(registerblockmem_1_cpp), .TOS(registerblockmem_1_tos),
    .OPC(registerblockmem_1_opc), .H(registerblockmem_1_h), .ABUS(registerblockmem_1_abus), .MBRin(MBRin),
    .ReadMBR(Fetch), .MDRin(MDRin), .ReadMDR(Read));  // open: MARout, MDRout, PCout, MBR_MPC
  Button Reset (.out(Reset_out));
  // Probe on registerblockmem_1_mar
  // Probe on registerblockmem_1_mdr
  // Probe on registerblockmem_1_pc
  // Probe on registerblockmem_1_sp
  // Probe on registerblockmem_1_lv
  // Probe on registerblockmem_1_cpp
  // Probe on registerblockmem_1_tos
  // Probe on registerblockmem_1_opc
  ALU32bit alu32bit_1 (
    .A(registerblockmem_1_abus), .O(alu32bit_1_o), .B(registerblockmem_1_bbus), .N(alu32bit_1_n),
    .Z(alu32bit_1_z), .in_3({F0, F1, ENA, ENB, INVA, INC}));
  shiftUnit shiftunit_1 (.SRA1(SRA1), .SLL8(SLL8), .IN(alu32bit_1_o), .OUT(shiftunit_1_out));
  Decoder #(.select(4)) decoder_1 (
    .out0(decoder_1_out0), .out1(decoder_1_out1), .out2(decoder_1_out2), .out3(decoder_1_out3),
    .out4(decoder_1_out4), .out5(decoder_1_out5), .out6(decoder_1_out6), .out7(decoder_1_out7),
    .out8(decoder_1_out8), .sel(B_Bus));  // open: out9, out10, out11, out12, out13, out14, out15, en
  LED N (.in(alu32bit_1_n));
  LED Z (.in(alu32bit_1_z));
  Button GO (.out(GO_out));

  // Other names for the same wires on the sheet: BSelect[3:0] = B_Bus; Control[5:0] = {F0, F1, ENA, ENB, INVA, INC};
  //   CSelect[8:0] = {iH, iOPC, iTOS, iCPP, iLV, iSP, iPC, iMDR, iMAR}; FE = Fetch; RD = Read;
  //   Shift[1:0] = {SLL8, SRA1}; WR = Write
endmodule
