// Logisim project mic1CPUv3.circ as structural Verilog: 1 circuit, main circuit main
module main (
  input  [31:0] MDRin,
  input  [7:0] MBRin,
  input  Program,
  input  SLL8,
  input  SRA1,
  input  F0,
  input  F1,
  input  ENA,
  input  ENB,
  input  INVA,
  input  INC,
  input  iH,
  input  iOPC,
  input  iTOS,
  input  iCPP,
  input  iLV,
  input  iSP,
  input  iPC,
  input  iMDR,
  input  iMAR,
  input  Wr,
  input  Rd,
  input  Fetch,
  input  [3:0] B_Bus,
  input  Hi,
  input  [7:0] Addr,
  input  Hi_2,
  input  [7:0] Addr_2,
  input  JMPC,
  input  JAMN,
  input  JAMZ
);

  wire ADD, CLK, decodepanel_1_b, decodepanel_1_b_cpp, decodepanel_1_b_lv, decodepanel_1_b_mbr,
       decodepanel_1_b_mbru, decodepanel_1_b_mdr, decodepanel_1_b_minus_1, decodepanel_1_b_minus_h,
       decodepanel_1_b_minus_h_minus_1, decodepanel_1_b_opc, decodepanel_1_b_pc, decodepanel_1_b_plus_1,
       decodepanel_1_b_sp, decodepanel_1_b_tos, decodepanel_1_berror, decodepanel_1_c_cpp, decodepanel_1_c_h,
       decodepanel_1_c_lv, decodepanel_1_c_mar, decodepanel_1_c_mdr, decodepanel_1_c_opc, decodepanel_1_c_pc,
       decodepanel_1_c_sp, decodepanel_1_c_tos, decodepanel_1_fe, decodepanel_1_h, decodepanel_1_h_and_b,
       decodepanel_1_h_or_b, decodepanel_1_h_plus_1, decodepanel_1_h_plus_b, decodepanel_1_h_plus_b_plus_1,
       decodepanel_1_m_one, decodepanel_1_minus_h, decodepanel_1_minus_h_minus_1, decodepanel_1_not_b,
       decodepanel_1_not_h, decodepanel_1_not_h_and_b, decodepanel_1_not_h_or_b, decodepanel_1_one,
       decodepanel_1_rd, decodepanel_1_shifterr, decodepanel_1_sll8, decodepanel_1_sra1, decodepanel_1_wr,
       decodepanel_1_zero, decoder_1_out0, decoder_1_out1, decoder_1_out2, decoder_1_out3, decoder_1_out4,
       decoder_1_out5, decoder_1_out6, decoder_1_out7, decoder_1_out8, FE, N, not_1_out, RD_t, Reset_out,
       WR_t, Z;
  wire [1:0] Shift;
  wire [3:0] BSelect;
  wire [5:0] Control;
  wire [7:0] registerblockmem_1_mbr;
  wire [8:0] controlstore_1_addrprobe, controlstore_1_nextaddr, CSelect;
  wire [23:0] Decode;
  wire [31:0] alu32bit_1_o, registerblockmem_1_abus, registerblockmem_1_bbus, registerblockmem_1_cpp,
       registerblockmem_1_h, registerblockmem_1_lv, registerblockmem_1_mar, registerblockmem_1_mdr,
       registerblockmem_1_opc, registerblockmem_1_pc, registerblockmem_1_sp, registerblockmem_1_tos,
       shiftunit_1_out;

  // Probe on registerblockmem_1_mbr
  // Probe on registerblockmem_1_h
  registerBlockMem registerblockmem_1 (
    .C_H(CSelect[8]), .C_TOS(CSelect[6]), .C_LV(CSelect[4]), .C_SP(CSelect[3]), .PC_B(decoder_1_out1),
    .C_MAR(CSelect[0]), .PC(registerblockmem_1_pc), .C_PC(CSelect[2]), .CBUS(shiftunit_1_out),
    .RST(Reset_out), .CPP_B(decoder_1_out6), .OPC_B(decoder_1_out8), .SP(registerblockmem_1_sp),
    .MAR(registerblockmem_1_mar), .TOS_B(decoder_1_out7), .LV_B(decoder_1_out5), .SP_B(decoder_1_out4),
    .MBR_B(decoder_1_out2), .C_MDR(CSelect[1]), .MBR(registerblockmem_1_mbr), .MDR_B(decoder_1_out0),
    .MBRU_B(decoder_1_out3), .CLK(CLK), .C_CPP(CSelect[5]), .C_OPC(CSelect[7]), .MDR(registerblockmem_1_mdr),
    .BBUS(registerblockmem_1_bbus), .LV(registerblockmem_1_lv), .CPP(registerblockmem_1_cpp),
    .TOS(registerblockmem_1_tos), .OPC(registerblockmem_1_opc), .H(registerblockmem_1_h),
    .ABUS(registerblockmem_1_abus), .MBRin(MBRin), .ReadMBR(FE), .MDRin(MDRin), .ReadMDR(RD_t));  // open: MARout, MDRout, PCout, MBR_MPC
  Button Reset (.out(Reset_out));
  // Probe on registerblockmem_1_mar
  // Probe on registerblockmem_1_mdr
  // Probe on registerblockmem_1_pc
  // Probe on registerblockmem_1_sp
  // Probe on registerblockmem_1_lv
  // Probe on registerblockmem_1_cpp
  // Probe on registerblockmem_1_tos
  // Probe on registerblockmem_1_opc
  ALU32bit alu32bit_1 (
    .A(registerblockmem_1_abus), .O(alu32bit_1_o), .B(registerblockmem_1_bbus), .N(N), .Z(Z), .in_3(Control));
  shiftUnit shiftunit_1 (.SRA1(Shift[0]), .SLL8(Shift[1]), .IN(alu32bit_1_o), .OUT(shiftunit_1_out));
  Decoder #(.select(4)) decoder_1 (
    .out0(decoder_1_out0), .out1(decoder_1_out1), .out2(decoder_1_out2), .out3(decoder_1_out3),
    .out4(decoder_1_out4), .out5(decoder_1_out5), .out6(decoder_1_out6), .out7(decoder_1_out7),
    .out8(decoder_1_out8), .sel(BSelect));  // open: out9, out10, out11, out12, out13, out14, out15, en
  Clock clock_1 (.out(CLK));
  LED led_1 (.in(decodepanel_1_b_mdr));
  LED led_2 (.in(decodepanel_1_b_pc));
  LED led_3 (.in(decodepanel_1_b_mbr));
  decodePanel decodepanel_1 (
    .one(decodepanel_1_one), .h_and_b(decodepanel_1_h_and_b), .not_h_and_b(decodepanel_1_not_h_and_b),
    .b_minus_h_minus_1(decodepanel_1_b_minus_h_minus_1), .minus_h(decodepanel_1_minus_h),
    .m_one(decodepanel_1_m_one), .zero(decodepanel_1_zero), .h_plus_b_plus_1(decodepanel_1_h_plus_b_plus_1),
    .b_minus_1(decodepanel_1_b_minus_1), .minus_h_minus_1(decodepanel_1_minus_h_minus_1),
    .not_h_or_b(decodepanel_1_not_h_or_b), .not_b(decodepanel_1_not_b), .h_plus_b(decodepanel_1_h_plus_b),
    .b_minus_h(decodepanel_1_b_minus_h), .b(decodepanel_1_b), .h_or_b(decodepanel_1_h_or_b),
    .b_plus_1(decodepanel_1_b_plus_1), .h_plus_1(decodepanel_1_h_plus_1), .h(decodepanel_1_h),
    .not_h(decodepanel_1_not_h), .Command(Decode), .FE(decodepanel_1_fe), .RD(decodepanel_1_rd),
    .WR(decodepanel_1_wr), .B_MDR(decodepanel_1_b_mdr), .B_MBR(decodepanel_1_b_mbr),
    .B_SP(decodepanel_1_b_sp), .B_CPP(decodepanel_1_b_cpp), .B_OPC(decodepanel_1_b_opc),
    .B_PC(decodepanel_1_b_pc), .B_MBRU(decodepanel_1_b_mbru), .B_LV(decodepanel_1_b_lv),
    .B_TOS(decodepanel_1_b_tos), .BError(decodepanel_1_berror), .C_MAR(decodepanel_1_c_mar),
    .C_MDR(decodepanel_1_c_mdr), .C_PC(decodepanel_1_c_pc), .C_LV(decodepanel_1_c_lv),
    .C_CPP(decodepanel_1_c_cpp), .C_TOS(decodepanel_1_c_tos), .C_OPC(decodepanel_1_c_opc),
    .C_H(decodepanel_1_c_h), .C_SP(decodepanel_1_c_sp), .SRA1(decodepanel_1_sra1), .SLL8(decodepanel_1_sll8),
    .ShiftErr(decodepanel_1_shifterr));
  LED led_4 (.in(decodepanel_1_b_mbru));
  LED led_5 (.in(decodepanel_1_b_sp));
  LED led_6 (.in(decodepanel_1_zero));
  LED led_7 (.in(decodepanel_1_b_lv));
  LED led_8 (.in(decodepanel_1_one));
  LED led_9 (.in(decodepanel_1_b_cpp));
  LED led_10 (.in(decodepanel_1_m_one));
  LED led_11 (.in(decodepanel_1_b_tos));
  LED led_12 (.in(decodepanel_1_h_and_b));
  LED led_13 (.in(decodepanel_1_b_opc));
  LED led_14 (.in(decodepanel_1_berror));
  LED led_15 (.in(decodepanel_1_h_or_b));
  // Probe on controlstore_1_addrprobe
  // Probe on controlstore_1_nextaddr
  LED led_16 (.in(decodepanel_1_h));
  LED led_17 (.in(decodepanel_1_h_plus_b));
  LED led_18 (.in(decodepanel_1_b));
  LED led_19 (.in(decodepanel_1_not_h));
  LED led_20 (.in(decodepanel_1_not_b));
  LED led_21 (.in(decodepanel_1_b_minus_h));
  LED led_22 (.in(decodepanel_1_h_plus_1));
  LED led_23 (.in(decodepanel_1_b_plus_1));
  LED led_24 (.in(decodepanel_1_h_plus_b_plus_1));
  LED led_25 (.in(decodepanel_1_minus_h));
  LED led_26 (.in(decodepanel_1_b_minus_1));
  LED led_27 (.in(decodepanel_1_b_minus_h_minus_1));
  LED led_28 (.in(decodepanel_1_not_h_and_b));
  LED led_29 (.in(decodepanel_1_minus_h_minus_1));
  LED led_30 (.in(decodepanel_1_not_h_or_b));
  controlStore controlstore_1 (
    .ADDR_IN({Hi, Addr}),
    .CNTRL({SLL8, SRA1, F0, F1, ENA, ENB, INVA, INC, iH, iOPC, iTOS, iCPP, iLV, iSP, iPC, iMDR, iMAR, Wr, Rd, Fetch, B_Bus}),
    .CLK(CLK), .N(N), .NEXT_JMP({Hi_2, Addr_2, JMPC, JAMN, JAMZ}), .Z(Z), .PROG(Program), .ADD_INSTR(ADD),
    .RESET(Reset_out), .CPU_Control({Shift, Control, CSelect, WR_t, RD_t, FE, BSelect}),
    .addrProbe(controlstore_1_addrprobe), .nextAddr(controlstore_1_nextaddr));  // open: MBR_IN
  LED led_31 (.in(decodepanel_1_c_mar));
  LED led_32 (.in(decodepanel_1_sra1));
  LED led_33 (.in(decodepanel_1_c_mdr));
  LED led_34 (.in(decodepanel_1_sll8));
  LED led_35 (.in(decodepanel_1_c_pc));
  LED led_36 (.in(decodepanel_1_shifterr));
  LED led_37 (.in(decodepanel_1_c_sp));
  Multiplexer #(.width(24), .enable("false")) multiplexer_1 (
    .in0({SLL8, SRA1, F0, F1, ENA, ENB, INVA, INC, iH, iOPC, iTOS, iCPP, iLV, iSP, iPC, iMDR, iMAR, Wr, Rd, Fetch, B_Bus}),
    .in1({Shift, Control, CSelect, WR_t, RD_t, FE, BSelect}), .out(Decode), .sel(not_1_out));
  LED led_38 (.in(decodepanel_1_c_lv));
  LED led_39 (.in(decodepanel_1_c_cpp));
  LED led_40 (.in(decodepanel_1_fe));
  LED led_41 (.in(decodepanel_1_c_tos));
  LED led_42 (.in(decodepanel_1_rd));
  LED led_43 (.in(decodepanel_1_c_opc));
  LED led_44 (.in(decodepanel_1_wr));
  LED led_45 (.in(decodepanel_1_c_h));
  not not_1 (not_1_out, Program);
  Button AddInstr (.out(ADD));

  // Other names for the same wires on the sheet: CNTL[23:0] = {SLL8, SRA1, F0, F1, ENA, ENB, INVA, INC, iH, iOPC, iTOS, iCPP, iLV, iSP, iPC, iMDR, iMAR, Wr, Rd, Fetch, B_Bus};
  //   MADDR[8:0] = {Hi, Addr}; NXT[11:0] = {Hi_2, Addr_2, JMPC, JAMN, JAMZ}
endmodule
