// Logisim project mic1ControlStore.circ as structural Verilog: 1 circuit, main circuit controlStore
module controlStore (
  input  [8:0] ADDR_IN,
  input  [11:0] NEXT_JMP,
  input  RESET,
  input  PROG,
  input  ADD_INSTR,
  input  [23:0] CNTRL,
  input  CLK,
  input  [7:0] MBR_IN,
  input  N,
  input  Z,
  output [8:0] addrProbe,
  output [23:0] CPU_Control,
  output [8:0] nextAddr
);

  wire and_1_out, and_2_out, CK, JMPC, not_2_out, NPR;
  wire [1:0] ram_1_dout_2;
  wire [8:0] or_1_out, register_1_q;
  wire [8:8] ram_1_dout;

  not not_1 (NPR, PROG);
  assign CK = NPR ? CLK : 1'bz;  // Controlled_Buffer controlled_buffer_1
  assign CK = PROG ? ADD_INSTR : 1'bz;  // Controlled_Buffer controlled_buffer_2
  assign nextAddr = JMPC ? {MBR_IN, 1'b0} : 9'bz;  // Controlled_Buffer controlled_buffer_3
  and and_1 (and_1_out, N, ram_1_dout_2[1]);
  Register #(.width(9)) register_1 (.D(nextAddr), .clk(CK), .Q(register_1_q), .clr(RESET));  // open: en
  assign nextAddr = not_2_out ? or_1_out : 9'bz;  // Controlled_Buffer controlled_buffer_4
  not not_2 (not_2_out, JMPC);
  or or_1 (or_1_out[8], and_1_out, and_2_out, ram_1_dout[8]);
  and and_2 (and_2_out, ram_1_dout_2[0], Z);
  assign addrProbe = PROG ? ADDR_IN : 9'bz;  // Controlled_Buffer controlled_buffer_5
  assign addrProbe = NPR ? register_1_q : 9'bz;  // Controlled_Buffer controlled_buffer_6
  RAM #(.addrWidth(9), .dataWidth(12), .trigger("falling"), .databus("bibus")) ram_1 (
    .addr(addrProbe), .we(PROG), .oe(NPR), .clk(CK), .din({NEXT_JMP[2:0], NEXT_JMP[11:3]}),
    .dout({JMPC, ram_1_dout_2, ram_1_dout[8], or_1_out[7:0]}));
  RAM #(.addrWidth(9), .dataWidth(24), .trigger("falling"), .databus("bibus")) ram_2 (
    .addr(addrProbe), .we(PROG), .oe(NPR), .clk(CK), .din(CNTRL), .dout(CPU_Control));

  // Other names for the same wires on the sheet: ADDR[8:0] = addrProbe; PR = PROG
endmodule
