// Logisim project mic1DecodePanel.circ as structural Verilog: 2 circuits, main circuit decodePanel
module decodePanel (
  input  [23:0] Command,
  output FE,
  output RD,
  output B_MDR,
  output not_b,
  output WR,
  output B_PC,
  output B_MBR,
  output B_MBRU,
  output B_SP,
  output B_LV,
  output not_h,
  output B_CPP,
  output B_TOS,
  output B_OPC,
  output zero,
  output h_or_b,
  output BError,
  output h_and_b,
  output not_h_or_b,
  output C_MAR,
  output C_MDR,
  output C_PC,
  output C_SP,
  output not_h_and_b,
  output C_LV,
  output C_CPP,
  output C_TOS,
  output C_OPC,
  output C_H,
  output b,
  output h_plus_b_plus_1,
  output one,
  output h_plus_b,
  output minus_h,
  output SRA1,
  output SLL8,
  output h_plus_1,
  output minus_h_minus_1,
  output m_one,
  output ShiftErr,
  output b_plus_1,
  output b_minus_1,
  output h,
  output b_minus_h_minus_1,
  output b_minus_h
);

  wire and_1_out, and_2_out, and_3_out, and_4_out, and_5_out, and_6_out, and_7_out, and_8_out, and_9_out,
       and_10_out, and_11_out, and_12_out, and_13_out, and_14_out, decoder_1_out9, decoder_1_out10,
       decoder_1_out11, decoder_1_out12, decoder_1_out13, decoder_1_out14, decoder_1_out15;

  and and_1 (and_1_out, ~Command[20], ~Command[21], ~Command[18]);  // AND_Gate
  and and_2 (and_2_out, ~Command[20], ~Command[21], ~Command[19], ~Command[17]);  // AND_Gate
  and and_3 (and_3_out, ~Command[20], ~Command[19], ~Command[18], ~Command[17]);  // AND_Gate
  or or_1 (zero, and_1_out, and_2_out, and_3_out, and_4_out, and_5_out);
  and and_4 (and_4_out, Command[21], ~Command[19], ~Command[18], ~Command[17], ~Command[16]);  // AND_Gate
  and and_5 (and_5_out, Command[20], Command[21], ~Command[19], ~Command[18], Command[17], Command[16]);  // AND_Gate
  and and_6 (and_6_out, ~Command[20], ~Command[21], ~Command[19], Command[18], Command[17]);  // AND_Gate
  and and_7 (and_7_out, ~Command[20], Command[21], ~Command[19], Command[18], ~Command[17]);  // AND_Gate
  or or_2 (b, and_6_out, and_7_out, and_8_out, and_9_out);
  and and_8 (and_8_out, Command[21], ~Command[19], Command[18], ~Command[17], ~Command[16]);  // AND_Gate
  and and_9 (and_9_out, Command[20], Command[21], ~Command[19], Command[18], Command[17], Command[16]);  // AND_Gate
  and and_10 (and_10_out, Command[20], ~Command[21], ~Command[18]);  // AND_Gate
  or or_3 (m_one, and_10_out, and_11_out, and_12_out);
  and and_11 (and_11_out, ~Command[20], Command[21], ~Command[19], Command[17]);  // AND_Gate
  and and_12 (and_12_out, Command[21], ~Command[19], ~Command[18], Command[17], ~Command[16]);  // AND_Gate
  and and_13 (and_13_out, ~Command[20], Command[21], Command[19], ~Command[18], ~Command[17]);  // AND_Gate
  or or_4 (h, and_13_out, and_14_out);
  and and_14 (and_14_out, Command[21], Command[19], ~Command[18], ~Command[17], ~Command[16]);  // AND_Gate
  and and_15 (not_b, Command[20], ~Command[21], Command[18]);  // AND_Gate
  and and_16 (not_h, ~Command[20], Command[21], Command[19], ~Command[18], Command[17]);  // AND_Gate
  and and_17 (h_or_b, ~Command[20], Command[21], Command[19], Command[18], ~Command[17]);  // AND_Gate
  and and_18 (h_and_b, ~Command[20], ~Command[21], Command[19], Command[18], ~Command[17]);  // AND_Gate
  and and_19 (not_h_or_b, ~Command[20], Command[21], Command[19], Command[18], Command[17]);  // AND_Gate
  and and_20 (not_h_and_b, ~Command[20], ~Command[21], Command[19], Command[18], Command[17]);  // AND_Gate
  and and_21 (h_plus_b_plus_1, Command[20], Command[21], Command[19], Command[18], ~Command[17], Command[16]);  // AND_Gate
  and and_22 (h_plus_b, Command[20], Command[21], Command[19], Command[18], ~Command[17], ~Command[16]);  // AND_Gate
  and and_23 (h_plus_1, Command[20], Command[21], Command[19], ~Command[18], ~Command[17], Command[16]);  // AND_Gate
  and and_24 (b_plus_1, Command[20], Command[21], ~Command[19], Command[18], ~Command[17], Command[16]);  // AND_Gate
  and and_25 (b_minus_h_minus_1, Command[20], Command[21], Command[19], Command[18], Command[17], ~Command[16]);  // AND_Gate
  and and_26 (one, Command[20], Command[21], ~Command[19], ~Command[18], ~Command[17], Command[16]);  // AND_Gate
  and and_27 (minus_h, Command[20], Command[21], Command[19], ~Command[18], Command[17], Command[16]);  // AND_Gate
  and and_28 (minus_h_minus_1, Command[20], Command[21], Command[19], ~Command[18], Command[17], ~Command[16]);  // AND_Gate
  and and_29 (b_minus_1, Command[20], Command[21], ~Command[19], Command[18], Command[17], ~Command[16]);  // AND_Gate
  and and_30 (b_minus_h, Command[20], Command[21], Command[19], Command[18], Command[17], Command[16]);
  Decoder #(.select(4), .enable("false")) decoder_1 (
    .out0(B_MDR), .out1(B_PC), .out2(B_MBR), .out3(B_MBRU), .out4(B_SP), .out5(B_LV), .out6(B_CPP),
    .out7(B_TOS), .out8(B_OPC), .out9(decoder_1_out9), .out10(decoder_1_out10), .out11(decoder_1_out11),
    .out12(decoder_1_out12), .out13(decoder_1_out13), .out14(decoder_1_out14), .out15(decoder_1_out15),
    .sel(Command[3:0]));
  Decoder #(.select(2), .enable("false")) decoder_2 (
    .out1(SRA1), .out2(SLL8), .out3(ShiftErr), .sel(Command[23:22]));  // open: out0
  or or_5 (BError, decoder_1_out9, decoder_1_out10, decoder_1_out11, decoder_1_out12, decoder_1_out13, decoder_1_out14, decoder_1_out15);

  assign C_CPP = Command[12];
  assign C_H = Command[15];
  assign C_LV = Command[11];
  assign C_MAR = Command[7];
  assign C_MDR = Command[8];
  assign C_OPC = Command[14];
  assign C_PC = Command[9];
  assign C_SP = Command[10];
  assign C_TOS = Command[13];
  assign FE = Command[4];
  assign RD = Command[5];
  assign WR = Command[6];

  // Other names for the same wires on the sheet: Control[5:0] = Command[21:16]; BSelect[3:0] = Command[3:0];
  //   CSelect[8:0] = Command[15:7]; Shift[1:0] = Command[23:22]
endmodule

module testDecode (
  input  SLL8,
  input  SRA1,
  input  F0,
  input  F1,
  input  ENA,
  input  ENB,
  input  INVA,
  input  INC,
  input  iH,
  input  iOPC,
  input  iTOS,
  input  iCPP,
  input  iLV,
  input  iSP,
  input  iPC,
  input  iMDR,
  input  iMAR,
  input  Wr,
  input  Rd,
  input  Fetch,
  input  [3:0] B_Bus
);

  wire button_1_out, button_2_out, decodepanel_1_b, decodepanel_1_b_cpp, decodepanel_1_b_lv,
       decodepanel_1_b_mbr, decodepanel_1_b_mbru, decodepanel_1_b_mdr, decodepanel_1_b_minus_1,
       decodepanel_1_b_minus_h, decodepanel_1_b_minus_h_minus_1, decodepanel_1_b_opc, decodepanel_1_b_pc,
       decodepanel_1_b_plus_1, decodepanel_1_b_sp, decodepanel_1_b_tos, decodepanel_1_berror,
       decodepanel_1_c_cpp, decodepanel_1_c_h, decodepanel_1_c_lv, decodepanel_1_c_mar, decodepanel_1_c_mdr,
       decodepanel_1_c_opc, decodepanel_1_c_pc, decodepanel_1_c_sp, decodepanel_1_c_tos, decodepanel_1_fe,
       decodepanel_1_h, decodepanel_1_h_and_b, decodepanel_1_h_or_b, decodepanel_1_h_plus_1,
       decodepanel_1_h_plus_b, decodepanel_1_h_plus_b_plus_1, decodepanel_1_m_one, decodepanel_1_minus_h,
       decodepanel_1_minus_h_minus_1, decodepanel_1_not_b, decodepanel_1_not_h, decodepanel_1_not_h_and_b,
       decodepanel_1_not_h_or_b, decodepanel_1_one, decodepanel_1_rd, decodepanel_1_shifterr,
       decodepanel_1_sll8, decodepanel_1_sra1, decodepanel_1_wr, decodepanel_1_zero;
  wire [5:0] counter_1_q;

  Button button_1 (.out(button_1_out));
  Button button_2 (.out(button_2_out));
  Counter #(.width(6), .max('h3f)) counter_1 (
    .clr(button_1_out), .clk(button_2_out), .Q(counter_1_q));  // open: load, up, count, D, carry
  decodePanel decodepanel_1 (
    .one(decodepanel_1_one), .h_and_b(decodepanel_1_h_and_b), .not_h_and_b(decodepanel_1_not_h_and_b),
    .b_minus_h_minus_1(decodepanel_1_b_minus_h_minus_1), .minus_h(decodepanel_1_minus_h),
    .m_one(decodepanel_1_m_one), .zero(decodepanel_1_zero), .h_plus_b_plus_1(decodepanel_1_h_plus_b_plus_1),
    .b_minus_1(decodepanel_1_b_minus_1), .minus_h_minus_1(decodepanel_1_minus_h_minus_1),
    .not_h_or_b(decodepanel_1_not_h_or_b), .not_b(decodepanel_1_not_b), .h_plus_b(decodepanel_1_h_plus_b),
    .b_minus_h(decodepanel_1_b_minus_h), .b(decodepanel_1_b), .h_or_b(decodepanel_1_h_or_b),
    .b_plus_1(decodepanel_1_b_plus_1), .h_plus_1(decodepanel_1_h_plus_1), .h(decodepanel_1_h),
    .not_h(decodepanel_1_not_h),
    .Command({SLL8, SRA1, F0, F1, ENA, ENB, INVA, INC, iH, iOPC, iTOS, iCPP, iLV, iSP, iPC, iMDR, iMAR, Wr, Rd, Fetch, B_Bus}),
    .FE(decodepanel_1_fe), .RD(decodepanel_1_rd), .WR(decodepanel_1_wr), .B_MDR(decodepanel_1_b_mdr),
    .B_MBR(decodepanel_1_b_mbr), .B_SP(decodepanel_1_b_sp), .B_CPP(decodepanel_1_b_cpp),
    .B_OPC(decodepanel_1_b_opc), .B_PC(decodepanel_1_b_pc), .B_MBRU(decodepanel_1_b_mbru),
    .B_LV(decodepanel_1_b_lv), .B_TOS(decodepanel_1_b_tos), .BError(decodepanel_1_berror),
    .C_MAR(decodepanel_1_c_mar), .C_MDR(decodepanel_1_c_mdr), .C_PC(decodepanel_1_c_pc),
    .C_LV(decodepanel_1_c_lv), .C_CPP(decodepanel_1_c_cpp), .C_TOS(decodepanel_1_c_tos),
    .C_OPC(decodepanel_1_c_opc), .C_H(decodepanel_1_c_h), .C_SP(decodepanel_1_c_sp),
    .SRA1(decodepanel_1_sra1), .SLL8(decodepanel_1_sll8), .ShiftErr(decodepanel_1_shifterr));
  LED led_1 (.in(decodepanel_1_b_lv));
  LED led_2 (.in(decodepanel_1_b_mdr));
  LED led_3 (.in(decodepanel_1_b_cpp));
  LED led_4 (.in(decodepanel_1_b_pc));
  LED led_5 (.in(decodepanel_1_b_mbr));
  LED led_6 (.in(decodepanel_1_b_tos));
  LED led_7 (.in(decodepanel_1_b_mbru));
  LED led_8 (.in(decodepanel_1_b_opc));
  LED led_9 (.in(decodepanel_1_b_sp));
  LED led_10 (.in(decodepanel_1_berror));
  LED led_11 (.in(decodepanel_1_h));
  LED led_12 (.in(decodepanel_1_b));
  LED led_13 (.in(decodepanel_1_zero));
  LED led_14 (.in(decodepanel_1_one));
  LED led_15 (.in(decodepanel_1_not_h));
  LED led_16 (.in(decodepanel_1_not_b));
  LED led_17 (.in(decodepanel_1_b_plus_1));
  LED led_18 (.in(decodepanel_1_m_one));
  LED led_19 (.in(decodepanel_1_h_plus_1));
  LED led_20 (.in(decodepanel_1_minus_h));
  LED led_21 (.in(decodepanel_1_b_minus_1));
  LED led_22 (.in(decodepanel_1_h_and_b));
  LED led_23 (.in(decodepanel_1_not_h_or_b));
  LED led_24 (.in(decodepanel_1_h_or_b));
  LED led_25 (.in(decodepanel_1_not_h_and_b));
  LED led_26 (.in(decodepanel_1_h_plus_b));
  LED led_27 (.in(decodepanel_1_b_minus_h));
  LED led_28 (.in(decodepanel_1_sra1));
  LED led_29 (.in(decodepanel_1_h_plus_b_plus_1));
  LED led_30 (.in(decodepanel_1_sll8));
  LED led_31 (.in(decodepanel_1_b_minus_h_minus_1));
  LED led_32 (.in(decodepanel_1_shifterr));
  LED led_33 (.in(decodepanel_1_minus_h_minus_1));
  LED led_34 (.in(decodepanel_1_c_lv));
  LED led_35 (.in(decodepanel_1_c_cpp));
  LED led_36 (.in(decodepanel_1_c_mar));
  LED led_37 (.in(decodepanel_1_c_mdr));
  LED led_38 (.in(decodepanel_1_c_tos));
  LED led_39 (.in(decodepanel_1_c_pc));
  LED led_40 (.in(decodepanel_1_c_opc));
  LED led_41 (.in(decodepanel_1_c_h));
  LED led_42 (.in(decodepanel_1_c_sp));
  LED led_43 (.in(decodepanel_1_fe));
  LED led_44 (.in(decodepanel_1_rd));
  LED led_45 (.in(decodepanel_1_wr));
endmodule
