// Logisim project multiplexer.circ as structural Verilog: 1 circuit, main circuit main
module main (
  input  I0,
  input  I1,
  input  I2,
  input  I3,
  input  I4,
  input  I5,
  input  I6,
  input  I7,
  input  A2,
  input  A1,
  input  A0,
  output out_12
);

  wire and_1_out, and_2_out, and_3_out, and_4_out, and_5_out, and_6_out, and_7_out, and_8_out, not_1_out,
       not_2_out, not_3_out;

  not not_1 (not_1_out, A2);
  not not_2 (not_2_out, A1);
  not not_3 (not_3_out, A0);
  and and_1 (and_1_out, I0, not_1_out, not_2_out, not_3_out);
  and and_2 (and_2_out, I1, not_1_out, not_2_out, A0);
  and and_3 (and_3_out, I2, not_1_out, A1, not_3_out);
  and and_4 (and_4_out, I3, not_1_out, A1, A0);
  and and_5 (and_5_out, I4, A2, not_2_out, not_3_out);
  and and_6 (and_6_out, I5, A2, not_2_out, A0);
  and and_7 (and_7_out, I6, A2, A1, not_3_out);
  and and_8 (and_8_out, I7, A2, A1, A0);
  or or_1 (out_12, and_1_out, and_2_out, and_3_out, and_4_out, and_5_out, and_6_out, and_7_out, and_8_out);
endmodule
