// Logisim project multiplexerNo9.circ as structural Verilog: 1 circuit, main circuit main
module main (
  input  I2,
  input  D,
  input  I6,
  input  A,
  input  B,
  input  C,
  output out_7
);

  wire and_1_out, and_2_out, and_3_out, and_4_out, and_5_out, and_6_out, and_7_out, and_8_out, not_1_out,
       not_2_out, not_3_out, not_4_out;

  not not_1 (not_1_out, D);
  not not_2 (not_2_out, A);
  not not_3 (not_3_out, B);
  not not_4 (not_4_out, C);
  and and_1 (and_1_out, D, not_2_out, not_3_out, not_4_out);
  and and_2 (and_2_out, 1'b1, not_2_out, not_3_out, C);
  and and_3 (and_3_out, I2, not_2_out, B, not_4_out);
  and and_4 (and_4_out, 1'b1, not_2_out, B, C);
  and and_5 (and_5_out, not_1_out, A, not_3_out, not_4_out);
  and and_6 (and_6_out, not_1_out, A, not_3_out, C);
  and and_7 (and_7_out, I6, A, B, not_4_out);
  and and_8 (and_8_out, D, A, B, C);
  or or_1 (out_7, and_1_out, and_2_out, and_3_out, and_4_out, and_5_out, and_6_out, and_7_out, and_8_out);
endmodule
