// Logisim project registerBlockNomem.circ as structural Verilog: 1 circuit, main circuit mic1RegBlockNomem
module mic1RegBlockNomem (
  input  C_MAR,
  input  C_MDR,
  input  MDR_B,
  input  C_PC,
  input  PC_B,
  input  MBR_B,
  input  MBRU_B,
  input  [31:0] CBUS,
  input  C_SP,
  input  SP_B,
  input  CLK,
  input  RST,
  input  C_LV,
  input  LV_B,
  input  C_CPP,
  input  CPP_B,
  input  C_TOS,
  input  TOS_B,
  input  C_OPC,
  input  OPC_B,
  input  C_H,
  output [31:0] MAR,
  output [31:0] MDR,
  output [31:0] PC,
  output [7:0] MBR,
  output [31:0] SP,
  output [31:0] BBUS,
  output [31:0] LV,
  output [31:0] CPP,
  output [31:0] TOS,
  output [31:0] OPC,
  output [31:0] H,
  output [31:0] ABUS
);

  wire CLR;
  wire [31:0] bit_extender_1_out, bit_extender_2_out;

  Register #(.width(32)) R_MAR (.D(CBUS), .en(C_MAR), .clk(CLK), .Q(MAR), .clr(CLR));
  Register #(.width(32)) R_MDR (.D(CBUS), .en(C_MDR), .clk(CLK), .Q(MDR), .clr(RST));
  Register #(.width(32)) R_PC (.D(CBUS), .en(C_PC), .clk(CLK), .Q(PC), .clr(RST));
  Register R_MBR (.clk(CLK), .Q(MBR), .clr(RST));  // open: D, en
  Register #(.width(32)) R_SP (.D(CBUS), .en(C_SP), .clk(CLK), .Q(SP), .clr(RST));
  Register #(.width(32)) R_LV (.D(CBUS), .en(C_LV), .clk(CLK), .Q(LV), .clr(RST));
  Register #(.width(32)) R_CPP (.D(CBUS), .en(C_CPP), .clk(CLK), .Q(CPP), .clr(RST));
  Register #(.width(32)) R_TOS (.D(CBUS), .en(C_TOS), .clk(CLK), .Q(TOS), .clr(RST));
  Register #(.width(32)) R_OPC (.D(CBUS), .en(C_OPC), .clk(CLK), .Q(OPC), .clr(RST));
  Register #(.width(32)) R_H (.D(CBUS), .en(C_H), .clk(CLK), .Q(ABUS), .clr(RST));
  assign bit_extender_1_out = {{24{MBR[7]}}, MBR};  // Bit_Extender bit_extender_1
  assign bit_extender_2_out = {{24{1'b0}}, MBR};  // Bit_Extender bit_extender_2
  assign BBUS = MDR_B ? MDR : 32'bz;  // Controlled_Buffer controlled_buffer_1
  assign BBUS = PC_B ? PC : 32'bz;  // Controlled_Buffer controlled_buffer_2
  assign BBUS = MBR_B ? bit_extender_1_out : 32'bz;  // Controlled_Buffer controlled_buffer_3
  assign BBUS = MBRU_B ? bit_extender_2_out : 32'bz;  // Controlled_Buffer controlled_buffer_4
  assign BBUS = SP_B ? SP : 32'bz;  // Controlled_Buffer controlled_buffer_5
  assign BBUS = LV_B ? LV : 32'bz;  // Controlled_Buffer controlled_buffer_6
  assign BBUS = CPP_B ? CPP : 32'bz;  // Controlled_Buffer controlled_buffer_7
  assign BBUS = TOS_B ? TOS : 32'bz;  // Controlled_Buffer controlled_buffer_8
  assign BBUS = OPC_B ? OPC : 32'bz;  // Controlled_Buffer controlled_buffer_9

  assign H = ABUS;
endmodule
