// Logisim project registerSet1.circ as structural Verilog: 2 circuits, main circuit registerSet
module registerSet (
  input  CLK,
  input  RST,
  input  [3:0] BSEL,
  input  RD,
  input  [31:0] MEMin,
  input  [31:0] CBUS,
  input  CH,
  input  COPC,
  input  CTOS,
  input  CCPP,
  input  CLV,
  input  CSP,
  input  CPC,
  input  CMDR,
  input  CMAR,
  output [31:0] MEMout,
  output [31:0] ABUS,
  output [31:0] BBUS
);

  wire CPP, LV, MBR, MBRU, MDR, not_1_out, OPC, or_1_out, PC, SP, TOS;
  wire [31:0] controlled_buffer_1_out, R_CPP_q, R_LV_q, R_OPC_q, R_PC_q, R_SP_q, R_TOS_q;

  assign controlled_buffer_1_out = not_1_out ? CBUS : 32'bz;  // Controlled_Buffer controlled_buffer_1
  not not_1 (not_1_out, RD);
  assign controlled_buffer_1_out = RD ? MEMin : 32'bz;  // Controlled_Buffer controlled_buffer_2
  Register #(.width(32)) R_MAR (.D(CBUS), .en(CMAR), .clk(CLK), .clr(RST));  // open: Q
  Register #(.width(32)) R_MDR (.D(controlled_buffer_1_out), .en(or_1_out), .clk(CLK), .Q(MEMout), .clr(RST));
  or or_1 (or_1_out, CMDR, RD);
  Register #(.width(32)) R_PC (.D(CBUS), .en(CPC), .clk(CLK), .Q(R_PC_q), .clr(RST));
  Register #(.width(32)) R_H (.D(CBUS), .en(CH), .clk(CLK), .Q(ABUS), .clr(RST));
  assign BBUS = MDR ? MEMout : 32'bz;  // Controlled_Buffer controlled_buffer_3
  assign BBUS = PC ? R_PC_q : 32'bz;  // Controlled_Buffer controlled_buffer_4
  Register #(.width(32)) R_SP (.D(CBUS), .en(CSP), .clk(CLK), .Q(R_SP_q), .clr(RST));
  Register #(.width(32)) R_LV (.D(CBUS), .en(CLV), .clk(CLK), .Q(R_LV_q), .clr(RST));
  assign BBUS = SP ? R_SP_q : 32'bz;  // Controlled_Buffer controlled_buffer_5
  assign BBUS = LV ? R_LV_q : 32'bz;  // Controlled_Buffer controlled_buffer_6
  Register #(.width(32)) R_CPP (.D(CBUS), .en(CCPP), .clk(CLK), .Q(R_CPP_q), .clr(RST));
  Register #(.width(32)) R_TOS (.D(CBUS), .en(CTOS), .clk(CLK), .Q(R_TOS_q), .clr(RST));
  Register #(.width(32)) R_OPC (.D(CBUS), .en(COPC), .clk(CLK), .Q(R_OPC_q), .clr(RST));
  assign BBUS = CPP ? R_CPP_q : 32'bz;  // Controlled_Buffer controlled_buffer_7
  assign BBUS = TOS ? R_TOS_q : 32'bz;  // Controlled_Buffer controlled_buffer_8
  assign BBUS = OPC ? R_OPC_q : 32'bz;  // Controlled_Buffer controlled_buffer_9
  Decoder #(.select(4)) decoder_1 (
    .out0(MDR), .out1(PC), .out2(MBR), .out3(MBRU), .out4(SP), .out5(LV), .out6(CPP), .out7(TOS), .out8(OPC),
    .sel(BSEL));  // open: out9, out10, out11, out12, out13, out14, out15, en
endmodule

module testRegisters (
  input  in_1,
  input  [31:0] in_2,
  input  in_3,
  input  in_4,
  input  in_5,
  input  in_6,
  input  in_7,
  input  in_8,
  input  in_9,
  input  in_10,
  input  in_11,
  input  [3:0] in_12
);

  wire alu32bit_1_n, alu32bit_1_z, button_1_out, button_2_out;
  wire [3:0] registerset_1_memout_2, registerset_1_memout_3, registerset_1_memout_4;
  wire [5:0] dipswitch_1_sw6;
  wire [31:0] alu32bit_1_o, registerset_1_abus, registerset_1_bbus, registerset_1_memout;

  Hex_Digit_Display hex_digit_display_1 (.value(registerset_1_memout[31:28]));  // open: dp
  Hex_Digit_Display hex_digit_display_2 (.value(registerset_1_memout[27:24]));  // open: dp
  Hex_Digit_Display hex_digit_display_3 (.value(registerset_1_memout_4));  // open: dp
  Hex_Digit_Display hex_digit_display_4 (.value(registerset_1_memout_3));  // open: dp
  DipSwitch #(.number(6)) dipswitch_1 (
    .sw1(dipswitch_1_sw6[5]), .sw2(dipswitch_1_sw6[4]), .sw3(dipswitch_1_sw6[3]), .sw4(dipswitch_1_sw6[2]),
    .sw5(dipswitch_1_sw6[1]), .sw6(dipswitch_1_sw6[0]));
  Hex_Digit_Display hex_digit_display_5 (.value(registerset_1_memout_2));  // open: dp
  Hex_Digit_Display hex_digit_display_6 (.value(registerset_1_memout[11:8]));  // open: dp
  Hex_Digit_Display hex_digit_display_7 (.value(registerset_1_memout[3:0]));  // open: dp
  Hex_Digit_Display hex_digit_display_8 (.value(registerset_1_memout[7:4]));  // open: dp
  Button button_1 (.out(button_1_out));
  registerSet registerset_1 (
    .CPC(in_5), .CLV(in_7), .CTOS(in_9), .CH(in_11), .COPC(in_10), .CCPP(in_8), .CSP(in_6),
    .CBUS(alu32bit_1_o), .MEMin(in_2), .RD(in_1), .BSEL(in_12), .RST(button_1_out), .CLK(button_2_out),
    .CMDR(in_4), .CMAR(in_3),
    .MEMout({registerset_1_memout[31:24], registerset_1_memout_4, registerset_1_memout_3, registerset_1_memout_2, registerset_1_memout[11:0]}),
    .ABUS(registerset_1_abus), .BBUS(registerset_1_bbus));
  ALU32bit alu32bit_1 (
    .A(registerset_1_abus), .O(alu32bit_1_o), .B(registerset_1_bbus), .N(alu32bit_1_n), .Z(alu32bit_1_z),
    .in_3(dipswitch_1_sw6));
  Button button_2 (.out(button_2_out));
  LED N (.in(alu32bit_1_n));
  LED Z (.in(alu32bit_1_z));
endmodule
