// Logisim project shiftUnit.circ as structural Verilog: 1 circuit, main circuit shiftUnit
module shiftUnit (
  input  [31:0] IN,
  input  SRA1,
  input  SLL8,
  output [31:0] OUT
);

  wire nor_1_out;
  wire [31:0] shifter_1_out, shifter_2_out;

  Shifter #(.width(32), .shift("ar")) shifter_1 (.in(IN), .\dist (5'b00001), .out(shifter_1_out));
  Shifter #(.width(32)) shifter_2 (.in(IN), .\dist (5'b01000), .out(shifter_2_out));
  assign OUT = SRA1 ? shifter_1_out : 32'bz;  // Controlled_Buffer controlled_buffer_1
  assign OUT = SLL8 ? shifter_2_out : 32'bz;  // Controlled_Buffer controlled_buffer_2
  assign OUT = nor_1_out ? IN : 32'bz;  // Controlled_Buffer controlled_buffer_3
  nor nor_1 (nor_1_out, SRA1, SLL8);
endmodule
