// Logisim project eightbits.circ as structural Verilog: 1 circuit, main circuit main
module main (
  input  in_1,
  input  in_2,
  input  in_3,
  input  in_4,
  input  [7:0] in_5,
  input  [7:0] in_6,
  output out_7,
  output [7:0] out_8,
  output out_9
);

  wire adder_1_cout, adder_2_cout, adder_3_cout, adder_4_cout, adder_6_cout, adder_7_cout, adder_8_cout,
       adder_9_cout, and_1_out, and_2_out, xor_1_out;

  and and_1 (and_1_out, in_4, in_3);
  or or_1 (out_9, and_1_out, and_2_out);
  xor xor_1 (xor_1_out, in_3, in_4);
  and and_2 (and_2_out, in_1, xor_1_out);
  xor xor_2 (out_7, in_1, xor_1_out);
  Adder #(.width(1)) adder_1 (.a(in_5[0]), .b(in_6[0]), .out(out_8[0]), .cin(in_2), .cout(adder_1_cout));
  Adder #(.width(1)) adder_2 (.a(in_5[1]), .b(in_6[1]), .out(out_8[1]), .cin(adder_1_cout), .cout(adder_2_cout));
  Adder #(.width(1)) adder_3 (.a(in_5[2]), .b(in_6[2]), .out(out_8[2]), .cin(adder_2_cout), .cout(adder_3_cout));
  Adder #(.width(1)) adder_4 (.a(in_5[3]), .b(in_6[3]), .out(out_8[3]), .cin(adder_3_cout), .cout(adder_4_cout));
  Adder #(.width(1)) adder_5 (.a(in_5[3]), .b(in_6[3]), .out(out_8[3]), .cin(adder_3_cout), .cout(adder_4_cout));
  Adder #(.width(1)) adder_6 (.a(in_5[4]), .b(in_6[4]), .out(out_8[4]), .cin(adder_4_cout), .cout(adder_6_cout));
  Adder #(.width(1)) adder_7 (.a(in_5[5]), .b(in_6[5]), .out(out_8[5]), .cin(adder_6_cout), .cout(adder_7_cout));
  Adder #(.width(1)) adder_8 (.a(in_5[6]), .b(in_6[6]), .out(out_8[6]), .cin(adder_7_cout), .cout(adder_8_cout));
  Adder #(.width(1)) adder_9 (.a(in_5[7]), .b(in_6[7]), .out(out_8[7]), .cin(adder_8_cout), .cout(adder_9_cout));
endmodule
