// Logisim project memory.circ as structural Verilog: 2 circuits, main circuit memory
module memory (
  input  S,
  input  R,
  output notQ,
  output Q
);

  nor nor_1 (notQ, S, Q);
  nor nor_2 (Q, notQ, R);
endmodule

module Dlatch (
  input  D,
  output out_2,
  output out_3
);

  wire and_1_out, and_2_out, Clk_out, not_1_out;

  not not_1 (not_1_out, D);
  Button Clk (.out(Clk_out));
  and and_1 (and_1_out, D, Clk_out);
  and and_2 (and_2_out, Clk_out, not_1_out);
  nor nor_1 (out_2, and_1_out, out_3);
  nor nor_2 (out_3, out_2, and_2_out);
endmodule
