// Logisim project onetotwo.circ as structural Verilog: 8 circuits, main circuit onebitnc
module onebitnc (
  input  A,
  input  B,
  output S,
  output C
);

  Adder #(.width(1)) adder_1 (.a(A), .b(B), .out(S), .cout(C));  // open: cin
endmodule

module twobitnc (
  input  [1:0] up,
  input  [1:0] down,
  output [1:0] S,
  output C
);

  wire onebitnc_1_c, onebitnc_2_c, onebitnc_2_s, onebitwc_1_c, onebitwc_1_s;

  onebitnc onebitnc_1 (.A(up[0]), .B(down[0]), .S(S[0]), .C(onebitnc_1_c));
  onebitnc onebitnc_2 (.A(up[1]), .B(down[1]), .S(onebitnc_2_s), .C(onebitnc_2_c));
  onebitwc onebitwc_1 (.A(up[1]), .B(down[1]), .S(onebitwc_1_s), .C(onebitwc_1_c));
  Multiplexer #(.enable("false")) multiplexer_1 (
    .in0(onebitnc_2_s), .in1(onebitwc_1_s), .out(S[1]), .sel(onebitnc_1_c));
  Multiplexer #(.enable("false")) multiplexer_2 (.in0(onebitnc_2_c), .in1(onebitwc_1_c), .out(C), .sel(onebitnc_1_c));
endmodule

module onebitwc (
  input  A,
  input  B,
  output S,
  output C
);

  Adder #(.width(1)) adder_1 (.a(A), .b(B), .out(S), .cin(1'b1), .cout(C));
endmodule

module twobitwc (
  input  [1:0] up,
  input  [1:0] down,
  output [1:0] s,
  output c
);

  wire onebitnc_1_c, onebitnc_1_s, onebitwc_1_c, onebitwc_2_c, onebitwc_2_s;

  onebitwc onebitwc_1 (.A(up[0]), .B(down[0]), .S(s[0]), .C(onebitwc_1_c));
  onebitnc onebitnc_1 (.A(up[1]), .B(down[1]), .S(onebitnc_1_s), .C(onebitnc_1_c));
  onebitwc onebitwc_2 (.A(up[1]), .B(down[1]), .S(onebitwc_2_s), .C(onebitwc_2_c));
  Multiplexer #(.enable("false")) multiplexer_1 (
    .in0(onebitnc_1_s), .in1(onebitwc_2_s), .out(s[1]), .sel(onebitwc_1_c));
  Multiplexer #(.enable("false")) multiplexer_2 (.in0(onebitnc_1_c), .in1(onebitwc_2_c), .out(c), .sel(onebitwc_1_c));
endmodule

module fourbitnc (
  input  [3:0] up,
  input  [3:0] down,
  output [3:0] s,
  output c
);

  wire twobitnc_1_c, twobitnc_2_c, twobitwc_1_c;
  wire [1:0] twobitnc_2_s, twobitwc_1_s;

  twobitnc twobitnc_1 (.up(up[1:0]), .down(down[1:0]), .S(s[1:0]), .C(twobitnc_1_c));
  twobitnc twobitnc_2 (.up(up[3:2]), .down(down[3:2]), .S(twobitnc_2_s), .C(twobitnc_2_c));
  twobitwc twobitwc_1 (.up(up[3:2]), .down(down[3:2]), .s(twobitwc_1_s), .c(twobitwc_1_c));
  Multiplexer #(.width(2), .enable("false")) multiplexer_1 (
    .in0(twobitnc_2_s), .in1(twobitwc_1_s), .out(s[3:2]), .sel(twobitnc_1_c));
  Multiplexer #(.enable("false")) multiplexer_2 (.in0(twobitnc_2_c), .in1(twobitwc_1_c), .out(c), .sel(twobitnc_1_c));
endmodule

module fourbitwc (
  input  [3:0] up,
  input  [3:0] down,
  output [3:0] out_3,
  output out_4
);

  wire twobitnc_1_c, twobitwc_1_c, twobitwc_2_c;
  wire [1:0] twobitnc_1_s, twobitwc_2_s;

  twobitwc twobitwc_1 (.up(up[1:0]), .down(down[1:0]), .s(out_3[1:0]), .c(twobitwc_1_c));
  twobitnc twobitnc_1 (.up(up[3:2]), .down(down[3:2]), .S(twobitnc_1_s), .C(twobitnc_1_c));
  twobitwc twobitwc_2 (.up(up[3:2]), .down(down[3:2]), .s(twobitwc_2_s), .c(twobitwc_2_c));
  Multiplexer #(.width(2), .enable("false")) multiplexer_1 (
    .in0(twobitnc_1_s), .in1(twobitwc_2_s), .out(out_3[3:2]), .sel(twobitwc_1_c));
  Multiplexer #(.enable("false")) multiplexer_2 (
    .in0(twobitnc_1_c), .in1(twobitwc_2_c), .out(out_4), .sel(twobitwc_1_c));
endmodule

module eightbitnc (
  input  [7:0] in_1,
  input  [7:0] in_2,
  output [7:0] s,
  output c
);

  wire fourbitnc_1_c, fourbitnc_2_c, fourbitwc_1_out_4;
  wire [3:0] fourbitnc_2_s, fourbitwc_1_out_3;

  fourbitnc fourbitnc_1 (.up(in_1[3:0]), .down(in_2[3:0]), .s(s[3:0]), .c(fourbitnc_1_c));
  fourbitnc fourbitnc_2 (.up(in_1[7:4]), .down(in_2[7:4]), .s(fourbitnc_2_s), .c(fourbitnc_2_c));
  fourbitwc fourbitwc_1 (.up(in_1[7:4]), .down(in_2[7:4]), .out_3(fourbitwc_1_out_3), .out_4(fourbitwc_1_out_4));
  Multiplexer #(.width(4), .enable("false")) multiplexer_1 (
    .in0(fourbitnc_2_s), .in1(fourbitwc_1_out_3), .out(s[7:4]), .sel(fourbitnc_1_c));
  Multiplexer #(.enable("false")) multiplexer_2 (
    .in0(fourbitnc_2_c), .in1(fourbitwc_1_out_4), .out(c), .sel(fourbitnc_1_c));
endmodule

module eightbitwc (
  input  [7:0] in_1,
  input  [7:0] in_2,
  output [7:0] out_3,
  output out_4
);

  wire fourbitnc_1_c, fourbitwc_1_out_4, fourbitwc_2_out_4;
  wire [3:0] fourbitnc_1_s, fourbitwc_2_out_3;

  fourbitwc fourbitwc_1 (.up(in_1[3:0]), .down(in_2[3:0]), .out_3(out_3[3:0]), .out_4(fourbitwc_1_out_4));
  fourbitnc fourbitnc_1 (.up(in_1[7:4]), .down(in_2[7:4]), .s(fourbitnc_1_s), .c(fourbitnc_1_c));
  fourbitwc fourbitwc_2 (.up(in_1[7:4]), .down(in_2[7:4]), .out_3(fourbitwc_2_out_3), .out_4(fourbitwc_2_out_4));
  Multiplexer #(.width(4), .enable("false")) multiplexer_1 (
    .in0(fourbitnc_1_s), .in1(fourbitwc_2_out_3), .out(out_3[7:4]), .sel(fourbitwc_1_out_4));
  Multiplexer #(.enable("false")) multiplexer_2 (
    .in0(fourbitnc_1_c), .in1(fourbitwc_2_out_4), .out(out_4), .sel(fourbitwc_1_out_4));
endmodule
